# Fritzing sketch Charger DC Tester (saved by Fritzing 0.9.3b)
breadboards: 1

parts:
  Part1 = Arduino Mega 2560 (Rev3) [part_number=MCU]
  R1 = Resistor [tolerance=±5% resistance=1k package=THT]
  R2 = Resistor [tolerance=±5% resistance=1k package=THT]
  D1 = Rectifier Diode [part_number=1N4001 package="300 mil [THT]"]
  Q1 = NPN-Transistor [package="TO92 [THT]"]
  Q2 = NPN-Transistor [package="TO92 [THT]"]
  J1 = Piezo Speaker
  U1 = RELAY [package=relay-t9a-2]
  U2 = RELAY [package=relay-t9a-2]
  JP1 = Header 5 [package=1x05-1mm-ra]
  JP2 = Header 5 [package=1x05-1mm-ra]
  X1 = USB Connectors [package=usb-b-pth-vertical]
  JP3 = Header 2 [package=jst-2-pth-ns]
  X2 = DB9 Connector [package=db9]

nets:
  TX1: Part1.D19/RX1, X2.3
  RX1: Part1.D18/TX1, X2.2
  GND: Part1.GND, Q1.E, Q2.E, JP1.5, JP2.5, X1.GND, X2.5
  buzzer: Part1.D9_PWM, R1.Pin_0
  relay: Part1.D8_PWM, R2.Pin_0
  TX0: Part1.D0_RX0, X1.VBUS
  RX0: Part1.D1_TX0, X1.D-
  sensor B: Part1.D2_PWM, JP2.4
  sensor A: Part1.D3_PWM, JP1.4
  N1: R1.Pin_1, Q2.B
  N2: R2.Pin_1, Q1.B
  N3: D1.cathode, U1.COIL1
  N4: D1.anode, Q1.C, U2.COIL2
  N5: Q2.C, J1.pin2
  24V: J1.pin1, X1.D+
  N6: U1.COIL2, U2.COIL1
  common chanel +: U1.MAIN, JP3.1
  chanel A +: U1.NC, JP1.1
  chanel B +: U1.NO, JP2.1
  common chanel -: U2.MAIN, JP3.2
  chanel A -: U2.NC, JP1.2
  chanel B -: U2.NO, JP2.2
  5V: JP1.3, JP2.3

notes:
  Charger DC Tester, 1.0
